// Logisim project Chips_avanzados.circ as structural Verilog: 6 circuits, main circuit HalfAdder
module HalfAdder (
  input  a,
  input  b,
  output Suma,
  output Carry
);

  xor xor_1 (Suma, a, b);
  and and_1 (Carry, a, b);
endmodule

module HalfAdder_det (
  input  a,
  input  b,
  output Suma,
  output Carry
);

  wire And_2_out, And_out, not_1_out, not_2_out;

  not not_1 (not_1_out, a);
  not not_2 (not_2_out, b);
  and And (And_out, not_1_out, b);
  and And_2 (And_2_out, a, not_2_out);
  or or_1 (Suma, And_out, And_2_out);
  and and_3 (Carry, a, b);
endmodule

module FullAdder (
  input  A,
  input  B,
  input  C,
  output Suma,
  output Carry
);

  wire and_1_out, and_2_out, and_3_out, and_4_out, and_5_out, and_6_out, and_7_out, and_8_out, and_9_out,
       and_10_out, and_11_out, and_12_out, and_13_out, and_14_out, and_15_out, and_16_out, not_1_out,
       not_2_out, not_3_out, or_1_out, or_2_out, or_3_out, or_4_out;

  not not_1 (not_1_out, A);
  not not_2 (not_2_out, B);
  not not_3 (not_3_out, C);
  and and_1 (and_1_out, not_1_out, not_2_out);
  and and_2 (and_2_out, not_1_out, B);
  and and_3 (and_3_out, A, not_2_out);
  and and_4 (and_4_out, A, B);
  and and_5 (and_5_out, not_1_out, B);
  and and_6 (and_6_out, A, not_2_out);
  and and_7 (and_7_out, A, B);
  and and_8 (and_8_out, A, B);
  and and_9 (and_9_out, and_1_out, C);
  and and_10 (and_10_out, and_2_out, not_3_out);
  and and_11 (and_11_out, and_3_out, not_3_out);
  and and_12 (and_12_out, and_4_out, C);
  and and_13 (and_13_out, and_5_out, C);
  and and_14 (and_14_out, and_6_out, C);
  and and_15 (and_15_out, and_7_out, not_3_out);
  and and_16 (and_16_out, and_8_out, C);
  or or_1 (or_1_out, and_9_out, and_10_out);
  or or_2 (or_2_out, or_1_out, and_11_out);
  or or_3 (or_3_out, and_13_out, and_14_out);
  or or_4 (or_4_out, or_3_out, and_15_out);
  or or_5 (Suma, or_2_out, and_12_out);
  or or_6 (Carry, or_4_out, and_16_out);
endmodule

module Adder16 (
  input  carryin,
  input  [15:0] A,
  input  [15:0] B,
  output [15:0] Suma,
  output Carryout
);

  wire fulladder_xor_1_cout, fulladder_xor_2_cout, fulladder_xor_3_cout, fulladder_xor_4_cout,
       fulladder_xor_5_cout, fulladder_xor_6_cout, fulladder_xor_7_cout, fulladder_xor_8_cout,
       fulladder_xor_9_cout, fulladder_xor_10_cout, fulladder_xor_11_cout, fulladder_xor_12_cout,
       fulladder_xor_13_cout, fulladder_xor_14_cout, fulladder_xor_15_cout;

  FullAdder_Xor fulladder_xor_1 (.Cin(carryin), .A(A[0]), .B(B[0]), .Sum(Suma[0]), .Cout(fulladder_xor_1_cout));
  FullAdder_Xor fulladder_xor_2 (
    .Cin(fulladder_xor_1_cout), .A(A[1]), .B(B[1]), .Sum(Suma[1]), .Cout(fulladder_xor_2_cout));
  FullAdder_Xor fulladder_xor_3 (
    .Cin(fulladder_xor_2_cout), .A(A[2]), .B(B[2]), .Sum(Suma[2]), .Cout(fulladder_xor_3_cout));
  FullAdder_Xor fulladder_xor_4 (
    .Cin(fulladder_xor_3_cout), .A(A[3]), .B(B[3]), .Sum(Suma[3]), .Cout(fulladder_xor_4_cout));
  FullAdder_Xor fulladder_xor_5 (
    .Cin(fulladder_xor_4_cout), .A(A[4]), .B(B[4]), .Sum(Suma[4]), .Cout(fulladder_xor_5_cout));
  FullAdder_Xor fulladder_xor_6 (
    .Cin(fulladder_xor_5_cout), .A(A[5]), .B(B[5]), .Sum(Suma[5]), .Cout(fulladder_xor_6_cout));
  FullAdder_Xor fulladder_xor_7 (
    .Cin(fulladder_xor_6_cout), .A(A[6]), .B(B[6]), .Sum(Suma[6]), .Cout(fulladder_xor_7_cout));
  FullAdder_Xor fulladder_xor_8 (
    .Cin(fulladder_xor_7_cout), .A(A[7]), .B(B[7]), .Sum(Suma[7]), .Cout(fulladder_xor_8_cout));
  FullAdder_Xor fulladder_xor_9 (
    .Cin(fulladder_xor_8_cout), .A(A[8]), .B(B[8]), .Sum(Suma[8]), .Cout(fulladder_xor_9_cout));
  FullAdder_Xor fulladder_xor_10 (
    .Cin(fulladder_xor_9_cout), .A(A[9]), .B(B[9]), .Sum(Suma[9]), .Cout(fulladder_xor_10_cout));
  FullAdder_Xor fulladder_xor_11 (
    .Cin(fulladder_xor_10_cout), .A(A[10]), .B(B[10]), .Sum(Suma[10]), .Cout(fulladder_xor_11_cout));
  FullAdder_Xor fulladder_xor_12 (
    .Cin(fulladder_xor_11_cout), .A(A[11]), .B(B[11]), .Sum(Suma[11]), .Cout(fulladder_xor_12_cout));
  FullAdder_Xor fulladder_xor_13 (
    .Cin(fulladder_xor_12_cout), .A(A[12]), .B(B[12]), .Sum(Suma[12]), .Cout(fulladder_xor_13_cout));
  FullAdder_Xor fulladder_xor_14 (
    .Cin(fulladder_xor_13_cout), .A(A[13]), .B(B[13]), .Sum(Suma[13]), .Cout(fulladder_xor_14_cout));
  FullAdder_Xor fulladder_xor_15 (
    .Cin(fulladder_xor_14_cout), .A(A[14]), .B(B[14]), .Sum(Suma[14]), .Cout(fulladder_xor_15_cout));
  FullAdder_Xor fulladder_xor_16 (.Cin(fulladder_xor_15_cout), .A(A[15]), .B(B[15]), .Sum(Suma[15]), .Cout(Carryout));
endmodule

module FullAdder_Xor (
  input  Cin,
  input  A,
  input  B,
  output Sum,
  output Cout
);

  wire and_1_out, and_2_out, xor_1_out;

  xor xor_1 (xor_1_out, A, B);
  and and_1 (and_1_out, A, B);
  and and_2 (and_2_out, xor_1_out, Cin);
  xor xor_2 (Sum, xor_1_out, Cin);
  or or_1 (Cout, and_2_out, and_1_out);
endmodule

module Inc16 (
  input  in_1,
  input  [15:0] A,
  output [15:0] out_3,
  output out_4
);

  wire fulladder_1_carry, fulladder_2_carry, fulladder_3_carry, fulladder_4_carry, fulladder_5_carry,
       fulladder_6_carry, fulladder_7_carry, fulladder_8_carry, fulladder_9_carry, fulladder_10_carry,
       fulladder_11_carry, fulladder_12_carry, fulladder_13_carry, fulladder_14_carry, fulladder_15_carry;

  FullAdder fulladder_1 (.A(in_1), .B(A[0]), .C(1'b1), .Suma(out_3[0]), .Carry(fulladder_1_carry));
  FullAdder fulladder_2 (.A(fulladder_1_carry), .B(A[1]), .C(1'b0), .Suma(out_3[1]), .Carry(fulladder_2_carry));
  FullAdder fulladder_3 (.A(fulladder_2_carry), .B(A[2]), .C(1'b0), .Suma(out_3[2]), .Carry(fulladder_3_carry));
  FullAdder fulladder_4 (.A(fulladder_3_carry), .B(A[3]), .C(1'b0), .Suma(out_3[3]), .Carry(fulladder_4_carry));
  FullAdder fulladder_5 (.A(fulladder_4_carry), .B(A[4]), .C(1'b0), .Suma(out_3[4]), .Carry(fulladder_5_carry));
  FullAdder fulladder_6 (.A(fulladder_5_carry), .B(A[5]), .C(1'b0), .Suma(out_3[5]), .Carry(fulladder_6_carry));
  FullAdder fulladder_7 (.A(fulladder_6_carry), .B(A[6]), .C(1'b0), .Suma(out_3[6]), .Carry(fulladder_7_carry));
  FullAdder fulladder_8 (.A(fulladder_7_carry), .B(A[7]), .C(1'b0), .Suma(out_3[7]), .Carry(fulladder_8_carry));
  FullAdder fulladder_9 (.A(fulladder_8_carry), .B(A[8]), .C(1'b0), .Suma(out_3[8]), .Carry(fulladder_9_carry));
  FullAdder fulladder_10 (.A(fulladder_9_carry), .B(A[9]), .C(1'b0), .Suma(out_3[9]), .Carry(fulladder_10_carry));
  FullAdder fulladder_11 (.A(fulladder_10_carry), .B(A[10]), .C(1'b0), .Suma(out_3[10]), .Carry(fulladder_11_carry));
  FullAdder fulladder_12 (.A(fulladder_11_carry), .B(A[11]), .C(1'b0), .Suma(out_3[11]), .Carry(fulladder_12_carry));
  FullAdder fulladder_13 (.A(fulladder_12_carry), .B(A[12]), .C(1'b0), .Suma(out_3[12]), .Carry(fulladder_13_carry));
  FullAdder fulladder_14 (.A(fulladder_13_carry), .B(A[13]), .C(1'b0), .Suma(out_3[13]), .Carry(fulladder_14_carry));
  FullAdder fulladder_15 (.A(fulladder_14_carry), .B(A[14]), .C(1'b0), .Suma(out_3[14]), .Carry(fulladder_15_carry));
  FullAdder fulladder_16 (.A(fulladder_15_carry), .B(A[15]), .C(1'b0), .Suma(out_3[15]), .Carry(out_4));
endmodule
