// Logisim project Chips_basicos.circ as structural Verilog
module And (
  input  A,
  input  B,
  output out
);

  wire nand_1_out;

  nand nand_1 (nand_1_out, A, B);
  not not_1 (out, nand_1_out);

  // Notes on the sheet:
  //   notAB
endmodule

module Not (
  input  in,
  output out
);

  not not_1 (out, in);
endmodule

module Or (
  input  a,
  input  b,
  output out
);

  wire and_1_out, not_1_out, not_2_out;

  not not_1 (not_1_out, a);
  not not_2 (not_2_out, b);
  and and_1 (and_1_out, not_1_out, not_2_out);
  not not_3 (out, and_1_out);

  // Notes on the sheet:
  //   notA
  //   notB
  //   And
endmodule

module Xor (
  input  a,
  input  b,
  output out
);

  wire and_1_out, and_2_out, not_1_out, not_2_out;

  not not_1 (not_1_out, a);
  not not_2 (not_2_out, b);
  and and_1 (and_1_out, a, not_2_out);
  and and_2 (and_2_out, not_1_out, b);
  or or_1 (out, and_1_out, and_2_out);

  // Notes on the sheet:
  //   And
  //   And
  //   Or
endmodule

module Mux (
  input  a,
  input  Sel,
  input  b,
  output out
);

  wire and_1_out, and_2_out, not_1_out;

  not not_1 (not_1_out, Sel);
  and and_1 (and_1_out, a, not_1_out);
  and and_2 (and_2_out, Sel, b);
  or or_1 (out, and_1_out, and_2_out);

  // Notes on the sheet:
  //   Sel
  //   Sel = 0  Out = a
  //   Sel = 1   Out = b
endmodule

module Dmux (
  input  in,
  input  Sel,
  output A,
  output B
);

  wire not_1_out;

  not not_1 (not_1_out, Sel);
  and and_1 (A, in, not_1_out);
  and and_2 (B, in, Sel);
endmodule

module Not16 (
  input  [15:0] in_1,
  output [15:0] out_2
);

  assign out_2[3:0] = ~in_1[3:0];  // NOT_Gate not_1, 4 bits wide
  assign out_2[7:4] = ~in_1[7:4];  // NOT_Gate not_2, 4 bits wide
  assign out_2[11:8] = ~in_1[11:8];  // NOT_Gate not_3, 4 bits wide
  assign out_2[15:12] = ~in_1[15:12];  // NOT_Gate not_4, 4 bits wide
endmodule

module And16 (
  input  [15:0] A,
  input  [15:0] B,
  output [15:0] out_3
);

  assign out_3[3:0] = A[3:0] & B[3:0];  // AND_Gate and_1, 4 bits wide
  assign out_3[7:4] = A[7:4] & B[7:4];  // AND_Gate and_2, 4 bits wide
  assign out_3[11:8] = A[11:8] & B[11:8];  // AND_Gate and_3, 4 bits wide
  assign out_3[15:12] = A[15:12] & B[15:12];  // AND_Gate and_4, 4 bits wide
endmodule

module Or16 (
  input  [15:0] in_1,
  input  [15:0] in_2,
  output [15:0] out_3
);

  assign out_3[3:0] = in_1[3:0] | in_2[3:0];  // OR_Gate or_1, 4 bits wide
  assign out_3[7:4] = in_1[7:4] | in_2[7:4];  // OR_Gate or_2, 4 bits wide
  assign out_3[11:8] = in_1[11:8] | in_2[11:8];  // OR_Gate or_3, 4 bits wide
  assign out_3[15:12] = in_1[15:12] | in_2[15:12];  // OR_Gate or_4, 4 bits wide
endmodule

module Mux16 (
  input  Sel,
  input  [15:0] A,
  input  [15:0] B,
  output [15:0] out_4
);

  Multiplexer #(.width(4), .enable("false")) multiplexer_1 (.in0(A[3:0]), .in1(B[3:0]), .out(out_4[3:0]), .sel(Sel));
  Multiplexer #(.width(4), .enable("false")) multiplexer_2 (.in0(A[7:4]), .in1(B[7:4]), .out(out_4[7:4]), .sel(Sel));
  Multiplexer #(.width(4), .enable("false")) multiplexer_3 (.in0(A[11:8]), .in1(B[11:8]), .out(out_4[11:8]), .sel(Sel));
  Multiplexer #(.width(4), .enable("false")) multiplexer_4 (
    .in0(A[15:12]), .in1(B[15:12]), .out(out_4[15:12]), .sel(Sel));
endmodule

module Or8Way (
  input  [7:0] Input,
  output Out
);

  wire or_1_out, or_2_out, or_3_out, or_4_out, or_5_out, or_7_out;

  or or_1 (or_1_out, Input[0], Input[1]);
  or or_2 (or_2_out, Input[2], Input[3]);
  or or_3 (or_3_out, Input[4], Input[5]);
  or or_4 (or_4_out, Input[6], Input[7]);
  or or_5 (or_5_out, or_1_out, or_2_out);
  or or_6 (Out, or_5_out, or_7_out);
  or or_7 (or_7_out, or_3_out, or_4_out);
endmodule

module Mux4Way16 (
  input  [15:0] A,
  input  [15:0] B,
  input  [1:0] Sel,
  input  [15:0] C,
  input  [1:0] Sel_2,
  input  [15:0] D,
  output [15:0] Out
);

  wire [15:0] multiplexer_1_out, multiplexer_2_out;

  Multiplexer #(.select(2), .width(16), .enable("false")) multiplexer_1 (
    .in0(A), .in3(B), .out(multiplexer_1_out), .sel(Sel));  // open: in1, in2
  Multiplexer #(.select(2), .width(16), .enable("false")) multiplexer_2 (
    .in0(C), .in3(D), .out(multiplexer_2_out), .sel(Sel));  // open: in1, in2
  Multiplexer #(.select(2), .width(16), .enable("false")) multiplexer_3 (
    .in0(multiplexer_1_out), .in3(multiplexer_2_out), .out(Out), .sel(Sel_2));  // open: in1, in2
endmodule

module Mux8Way16 (
  input  [15:0] A,
  input  [15:0] B,
  input  [15:0] C,
  input  [15:0] D,
  input  [2:0] Sel,
  input  [15:0] E,
  input  [15:0] F,
  input  [15:0] G,
  input  [15:0] H,
  output [15:0] Out
);

  wire [15:0] multiplexer_1_out, multiplexer_2_out, multiplexer_3_out, multiplexer_4_out, multiplexer_5_out,
       multiplexer_6_out;

  Multiplexer #(.width(16), .enable("false")) multiplexer_1 (.in0(A), .in1(B), .out(multiplexer_1_out), .sel(Sel[0]));
  Multiplexer #(.width(16), .enable("false")) multiplexer_2 (.in0(C), .in1(D), .out(multiplexer_2_out), .sel(Sel[0]));
  Multiplexer #(.width(16), .enable("false")) multiplexer_3 (.in0(E), .in1(F), .out(multiplexer_3_out), .sel(Sel[0]));
  Multiplexer #(.width(16), .enable("false")) multiplexer_4 (.in0(G), .in1(H), .out(multiplexer_4_out), .sel(Sel[0]));
  Multiplexer #(.width(16), .enable("false")) multiplexer_5 (
    .in0(multiplexer_1_out), .in1(multiplexer_2_out), .out(multiplexer_5_out), .sel(Sel[1]));
  Multiplexer #(.width(16), .enable("false")) multiplexer_6 (
    .in0(multiplexer_3_out), .in1(multiplexer_4_out), .out(multiplexer_6_out), .sel(Sel[1]));
  Multiplexer #(.width(16), .enable("false")) multiplexer_7 (
    .in0(multiplexer_5_out), .in1(multiplexer_6_out), .out(Out), .sel(Sel[2]));
endmodule

module Dmux4Way (
  input  Input,
  input  [2:0] Sel_0,
  input  [2:0] Sel_0_2,
  input  [2:0] Sel_1,
  output A,
  output B,
  output C,
  output D,
  output E,
  output F,
  output G,
  output H
);

  wire demultiplexer_1_out3, demultiplexer_1_out5, demultiplexer_2_out0, demultiplexer_2_out7,
       demultiplexer_3_out0, demultiplexer_3_out7;

  Demultiplexer #(.select(3), .enable("false")) demultiplexer_1 (
    .out3(demultiplexer_1_out3), .out5(demultiplexer_1_out5), .in(Input), .sel(Sel_1));  // open: out0, out1, out2, out4, out6, out7
  Demultiplexer #(.select(3), .enable("false")) demultiplexer_2 (
    .out0(demultiplexer_2_out0), .out7(demultiplexer_2_out7), .in(demultiplexer_1_out3), .sel(Sel_0));  // open: out1, out2, out3, out4, out5, out6
  Demultiplexer #(.select(3), .enable("false")) demultiplexer_3 (
    .out0(demultiplexer_3_out0), .out7(demultiplexer_3_out7), .in(demultiplexer_1_out5), .sel(Sel_0));  // open: out1, out2, out3, out4, out5, out6
  Demultiplexer #(.select(3), .enable("false")) demultiplexer_4 (
    .out2(A), .out5(B), .in(demultiplexer_2_out0), .sel(Sel_0_2));  // open: out0, out1, out3, out4, out6, out7
  Demultiplexer #(.select(3), .enable("false")) demultiplexer_5 (
    .out2(C), .out5(D), .in(demultiplexer_2_out7), .sel(Sel_0_2));  // open: out0, out1, out3, out4, out6, out7
  Demultiplexer #(.select(3), .enable("false")) demultiplexer_6 (
    .out2(E), .out5(F), .in(demultiplexer_3_out0), .sel(Sel_0_2));  // open: out0, out1, out3, out4, out6, out7
  Demultiplexer #(.select(3), .enable("false")) demultiplexer_7 (
    .out2(G), .out5(H), .in(demultiplexer_3_out7), .sel(Sel_0_2));  // open: out0, out1, out3, out4, out6, out7
endmodule

module Dmux8Way (
  input  Input,
  input  [2:0] Sel_1,
  input  [2:0] Sel_0,
  input  [2:0] Sel_2,
  output A,
  output B,
  output C,
  output D,
  output E,
  output F,
  output G,
  output H
);

  wire demultiplexer_1_out3, demultiplexer_1_out5, demultiplexer_2_out0, demultiplexer_2_out7,
       demultiplexer_3_out0, demultiplexer_3_out7;

  Demultiplexer #(.select(3), .enable("false")) demultiplexer_1 (
    .out3(demultiplexer_1_out3), .out5(demultiplexer_1_out5), .in(Input), .sel(Sel_2));  // open: out0, out1, out2, out4, out6, out7
  Demultiplexer #(.select(3), .enable("false")) demultiplexer_2 (
    .out0(demultiplexer_2_out0), .out7(demultiplexer_2_out7), .in(demultiplexer_1_out3), .sel(Sel_1));  // open: out1, out2, out3, out4, out5, out6
  Demultiplexer #(.select(3), .enable("false")) demultiplexer_3 (
    .out0(demultiplexer_3_out0), .out7(demultiplexer_3_out7), .in(demultiplexer_1_out5), .sel(Sel_1));  // open: out1, out2, out3, out4, out5, out6
  Demultiplexer #(.select(3), .enable("false")) demultiplexer_4 (
    .out2(A), .out5(B), .in(demultiplexer_2_out0), .sel(Sel_0));  // open: out0, out1, out3, out4, out6, out7
  Demultiplexer #(.select(3), .enable("false")) demultiplexer_5 (
    .out2(C), .out5(D), .in(demultiplexer_2_out7), .sel(Sel_0));  // open: out0, out1, out3, out4, out6, out7
  Demultiplexer #(.select(3), .enable("false")) demultiplexer_6 (
    .out2(E), .out5(F), .in(demultiplexer_3_out0), .sel(Sel_0));  // open: out0, out1, out3, out4, out6, out7
  Demultiplexer #(.select(3), .enable("false")) demultiplexer_7 (
    .out2(G), .out5(H), .in(demultiplexer_3_out7), .sel(Sel_0));  // open: out0, out1, out3, out4, out6, out7
endmodule
